# Fritzing sketch electronics_v0 (saved by Fritzing 0.9.3b)
breadboards: 1

parts:
  Arduino = Arduino Leonardo (Rev3b)
  engineStbd = SLIDER [package=slider]
  Rudder = POT [package=alps_pot]
  enginePort = SLIDER [package=slider]
  play = Square Pushbutton
  R1 = Resistor [tolerance=±5% resistance=10k package=THT]
  view = Square Pushbutton
  R2 = Resistor [tolerance=±5% resistance=10k package=THT]
  speed = Square Pushbutton
  R3 = Resistor [tolerance=±5% resistance=10k package=THT]
  horn = Square Pushbutton
  R4 = Resistor [tolerance=±5% resistance=10k package=THT]

nets:
  N1: Arduino.D0/RX, play.leg1
  N2: Arduino.D1/TX, view.leg1
  N3: Arduino.GND, engineStbd.A, Rudder.A, enginePort.A, R1.Pin_0, R2.Pin_0, R3.Pin_0, R4.Pin_0
  N4: Arduino.A0, enginePort.S
  N5: Arduino.A1, engineStbd.S
  N6: Arduino.A2, Rudder.S
  N7: Arduino.AREF, Rudder.E, enginePort.E
  N8: Arduino.SDA, speed.leg1
  N9: Arduino.SCL, horn.leg1
  N10: play.leg0, R1.Pin_1
  N11: view.leg0, R2.Pin_1
  N12: speed.leg0, R3.Pin_1
  N13: horn.leg0, R4.Pin_1
